// Logisim project logisim.circ as structural Verilog: 5 circuits, main circuit main
module main (
  input  in_1,
  input  in_2,
  input  in_3,
  input  in_4,
  input  in_5,
  input  in_6,
  input  in_7,
  input  in_8,
  input  in_9,
  input  in_10,
  input  in_11,
  input  in_12,
  input  [7:0] in_13,
  input  [7:0] in_14,
  input  [7:0] in_15,
  input  [7:0] in_16,
  input  [7:0] in_17,
  input  [7:0] Mux8,
  input  [7:0] in_19,
  input  in_20,
  input  [7:0] in_21,
  input  [7:0] in_22,
  output [7:0] out_23,
  output [7:0] out_24,
  output [7:0] out_25,
  output [7:0] out_26,
  output [7:0] out_27
);

  wire nand_1_out, nand_2_out, nand_3_out, nand_12_out, nand_13_out, nand_14_out, nand_15_out, nand_16_out,
       nand_17_out, nand_18_out, nand_19_out, nand_20_out, nand_21_out, nand_22_out, nand_23_out,
       nand_24_out, nand_25_out, nand_26_out, nand_27_out, nand_28_out, nand_37_out, nand_38_out,
       nand_47_out, nand_48_out, nand_49_out, nand_50_out, nand_51_out, nand_52_out, nand_53_out,
       nand_54_out, nand_55_out, nand_56_out, nand_57_out, nand_58_out, nand_59_out, nand_60_out,
       nand_61_out, nand_62_out, nand_63_out, nand_64_out, nand_65_out, nand_66_out, nand_67_out,
       nand_68_out, nand_69_out, nand_70_out, nand_71_out, nand_72_out, nand_73_out, nand_74_out,
       nand_75_out, nand_76_out, nand_77_out, nand_78_out, nand_95_out, nand_96_out, nand_97_out, or_1_out;

  // Probe on nand_1_out
  nand nand_1 (nand_1_out, in_4, in_4);
  nand nand_2 (nand_2_out, in_9, in_11);
  or or_1 (or_1_out, in_9, in_11);
  nand nand_3 (nand_3_out, nand_2_out, or_1_out);
  nand nand_4 (out_25[0], in_15[0], in_15[0]);
  nand nand_5 (out_25[1], in_15[1], in_15[1]);
  nand nand_6 (out_25[2], in_15[2], in_15[2]);
  nand nand_7 (out_25[3], in_15[3], in_15[3]);
  nand nand_8 (out_25[4], in_15[4], in_15[4]);
  nand nand_9 (out_25[5], in_15[5], in_15[5]);
  nand nand_10 (out_25[6], in_15[6], in_15[6]);
  nand nand_11 (out_25[7], in_15[7], in_15[7]);
  nand nand_12 (nand_12_out, in_19[0], in_19[0]);
  nand nand_13 (nand_13_out, in_19[1], in_19[1]);
  nand nand_14 (nand_14_out, in_19[2], in_19[2]);
  nand nand_15 (nand_15_out, in_19[3], in_19[3]);
  nand nand_16 (nand_16_out, in_19[4], in_19[4]);
  nand nand_17 (nand_17_out, in_19[5], in_19[5]);
  nand nand_18 (nand_18_out, in_19[6], in_19[6]);
  nand nand_19 (nand_19_out, in_19[7], in_19[7]);
  nand nand_20 (nand_20_out, in_21[0], in_21[0]);
  nand nand_21 (nand_21_out, in_21[1], in_21[1]);
  nand nand_22 (nand_22_out, in_21[2], in_21[2]);
  nand nand_23 (nand_23_out, in_21[3], in_21[3]);
  nand nand_24 (nand_24_out, in_21[4], in_21[4]);
  nand nand_25 (nand_25_out, in_21[5], in_21[5]);
  nand nand_26 (nand_26_out, in_21[6], in_21[6]);
  nand nand_27 (nand_27_out, in_21[7], in_21[7]);
  // Probe on nand_28_out
  nand nand_28 (nand_28_out, nand_3_out, nand_3_out);
  nand nand_29 (out_26[0], nand_12_out, nand_20_out);
  nand nand_30 (out_26[1], nand_13_out, nand_21_out);
  nand nand_31 (out_26[2], nand_14_out, nand_22_out);
  nand nand_32 (out_26[3], nand_15_out, nand_23_out);
  nand nand_33 (out_26[4], nand_16_out, nand_24_out);
  nand nand_34 (out_26[5], nand_17_out, nand_25_out);
  nand nand_35 (out_26[6], nand_18_out, nand_26_out);
  nand nand_36 (out_26[7], nand_19_out, nand_27_out);
  nand nand_37 (nand_37_out, in_2, in_5);
  // Probe on nand_38_out
  nand nand_38 (nand_38_out, nand_37_out, nand_37_out);
  nand nand_39 (out_24[0], in_14[0], in_17[0]);
  nand nand_40 (out_24[1], in_14[1], in_17[1]);
  nand nand_41 (out_24[2], in_14[2], in_17[2]);
  nand nand_42 (out_24[3], in_14[3], in_17[3]);
  nand nand_43 (out_24[4], in_14[4], in_17[4]);
  nand nand_44 (out_24[5], in_14[5], in_17[5]);
  nand nand_45 (out_24[6], in_14[6], in_17[6]);
  nand nand_46 (out_24[7], in_14[7], in_17[7]);
  nand nand_47 (nand_47_out, in_3, in_3);
  nand nand_48 (nand_48_out, in_6, in_6);
  nand nand_49 (nand_49_out, in_10, in_10);
  nand nand_50 (nand_50_out, in_20, in_20);
  nand nand_51 (nand_51_out, in_8, nand_49_out);
  nand nand_52 (nand_52_out, in_10, in_12);
  nand nand_53 (nand_53_out, in_13[0], in_16[0]);
  nand nand_54 (nand_54_out, in_13[1], in_16[1]);
  nand nand_55 (nand_55_out, in_13[2], in_16[2]);
  nand nand_56 (nand_56_out, in_13[3], in_16[3]);
  nand nand_57 (nand_57_out, in_13[4], in_16[4]);
  nand nand_58 (nand_58_out, in_13[5], in_16[5]);
  nand nand_59 (nand_59_out, in_13[6], in_16[6]);
  nand nand_60 (nand_60_out, in_13[7], in_16[7]);
  nand nand_61 (nand_61_out, Mux8[0], nand_50_out);
  nand nand_62 (nand_62_out, Mux8[1], nand_50_out);
  nand nand_63 (nand_63_out, Mux8[2], nand_50_out);
  nand nand_64 (nand_64_out, Mux8[3], nand_50_out);
  nand nand_65 (nand_65_out, Mux8[4], nand_50_out);
  nand nand_66 (nand_66_out, Mux8[5], nand_50_out);
  nand nand_67 (nand_67_out, Mux8[6], nand_50_out);
  nand nand_68 (nand_68_out, Mux8[7], nand_50_out);
  nand nand_69 (nand_69_out, in_20, in_22[0]);
  nand nand_70 (nand_70_out, in_20, in_22[1]);
  nand nand_71 (nand_71_out, in_20, in_22[2]);
  nand nand_72 (nand_72_out, in_20, in_22[3]);
  nand nand_73 (nand_73_out, in_20, in_22[4]);
  nand nand_74 (nand_74_out, in_20, in_22[5]);
  nand nand_75 (nand_75_out, in_20, in_22[6]);
  nand nand_76 (nand_76_out, in_20, in_22[7]);
  // Probe on nand_77_out
  nand nand_77 (nand_77_out, nand_47_out, nand_48_out);
  // Probe on nand_78_out
  nand nand_78 (nand_78_out, nand_51_out, nand_52_out);
  nand nand_79 (out_23[0], nand_53_out, nand_53_out);
  nand nand_80 (out_23[1], nand_54_out, nand_54_out);
  nand nand_81 (out_23[2], nand_55_out, nand_55_out);
  nand nand_82 (out_23[3], nand_56_out, nand_56_out);
  nand nand_83 (out_23[4], nand_57_out, nand_57_out);
  nand nand_84 (out_23[5], nand_58_out, nand_58_out);
  nand nand_85 (out_23[6], nand_59_out, nand_59_out);
  nand nand_86 (out_23[7], nand_60_out, nand_60_out);
  nand nand_87 (out_27[0], nand_61_out, nand_70_out);
  nand nand_88 (out_27[1], nand_62_out, nand_69_out);
  nand nand_89 (out_27[2], nand_63_out, nand_71_out);
  nand nand_90 (out_27[3], nand_64_out, nand_72_out);
  nand nand_91 (out_27[4], nand_65_out, nand_73_out);
  nand nand_92 (out_27[5], nand_66_out, nand_74_out);
  nand nand_93 (out_27[6], nand_67_out, nand_75_out);
  nand nand_94 (out_27[7], nand_68_out, nand_76_out);
  nand nand_95 (nand_95_out, in_1, in_1);
  nand nand_96 (nand_96_out, nand_95_out, in_7);
  nand nand_97 (nand_97_out, in_1, in_7);
  // Probe on nand_96_out
  // Probe on nand_97_out

  // Notes on the sheet:
  //   Not
  //   Or8
  //   Not8
  //   And
  //   Nand8
  //   Or
  //   Mux
  //   And8
endmodule

module Mux4way4 (
  input  [3:0] a,
  input  [3:0] b,
  input  [3:0] c,
  input  [3:0] d,
  input  [1:0] sel,
  output [3:0] out_6
);

  wire nand_1_out, nand_2_out, nand_3_out, nand_4_out, nand_5_out, nand_6_out, nand_7_out, nand_8_out,
       nand_9_out, nand_10_out, nand_11_out, nand_12_out, nand_13_out, nand_14_out, nand_15_out, nand_16_out,
       nand_17_out, nand_18_out, nand_19_out, nand_20_out, nand_21_out, nand_22_out, nand_23_out,
       nand_24_out, nand_25_out, nand_26_out, nand_27_out, nand_28_out, nand_29_out, nand_30_out,
       nand_31_out, nand_32_out, nand_33_out, nand_34_out;

  nand nand_1 (nand_1_out, sel[1], sel[1]);
  nand nand_2 (nand_2_out, a[0], nand_1_out);
  nand nand_3 (nand_3_out, a[1], nand_1_out);
  nand nand_4 (nand_4_out, a[2], nand_1_out);
  nand nand_5 (nand_5_out, a[3], nand_1_out);
  nand nand_6 (nand_6_out, b[0], nand_1_out);
  nand nand_7 (nand_7_out, b[1], nand_1_out);
  nand nand_8 (nand_8_out, b[2], nand_1_out);
  nand nand_9 (nand_9_out, b[3], nand_1_out);
  nand nand_10 (nand_10_out, c[0], sel[1]);
  nand nand_11 (nand_11_out, c[1], sel[1]);
  nand nand_12 (nand_12_out, c[2], sel[1]);
  nand nand_13 (nand_13_out, c[3], sel[1]);
  nand nand_14 (nand_14_out, d[0], sel[1]);
  nand nand_15 (nand_15_out, d[1], sel[1]);
  nand nand_16 (nand_16_out, d[2], sel[1]);
  nand nand_17 (nand_17_out, d[3], sel[1]);
  nand nand_18 (nand_18_out, nand_2_out, nand_7_out);
  nand nand_19 (nand_19_out, nand_3_out, nand_6_out);
  nand nand_20 (nand_20_out, nand_4_out, nand_8_out);
  nand nand_21 (nand_21_out, nand_5_out, nand_9_out);
  nand nand_22 (nand_22_out, nand_10_out, nand_15_out);
  nand nand_23 (nand_23_out, nand_11_out, nand_14_out);
  nand nand_24 (nand_24_out, nand_12_out, nand_16_out);
  nand nand_25 (nand_25_out, nand_13_out, nand_17_out);
  nand nand_26 (nand_26_out, sel[0], nand_22_out);
  nand nand_27 (nand_27_out, sel[0], nand_23_out);
  nand nand_28 (nand_28_out, sel[0], nand_24_out);
  nand nand_29 (nand_29_out, sel[0], nand_25_out);
  nand nand_30 (nand_30_out, sel[0], sel[0]);
  nand nand_31 (nand_31_out, nand_18_out, nand_30_out);
  nand nand_32 (nand_32_out, nand_19_out, nand_30_out);
  nand nand_33 (nand_33_out, nand_20_out, nand_30_out);
  nand nand_34 (nand_34_out, nand_21_out, nand_30_out);
  nand nand_35 (out_6[0], nand_31_out, nand_26_out);
  nand nand_36 (out_6[1], nand_32_out, nand_27_out);
  nand nand_37 (out_6[2], nand_33_out, nand_28_out);
  nand nand_38 (out_6[3], nand_34_out, nand_29_out);

  // Notes on the sheet:
  //   Mux4
endmodule

module Dmux4way4 (
  input  [3:0] in_1,
  input  [1:0] sel,
  output [3:0] out_3,
  output [3:0] out_4,
  output [3:0] out_5,
  output [3:0] out_6
);

  wire nand_1_out, nand_2_out, nand_3_out, nand_4_out, nand_5_out, nand_6_out, nand_7_out, nand_8_out,
       nand_9_out, nand_10_out, nand_11_out, nand_12_out, nand_13_out, nand_14_out, nand_15_out, nand_16_out,
       nand_17_out, nand_18_out, nand_19_out, nand_20_out, nand_21_out, nand_22_out, nand_23_out,
       nand_24_out, nand_25_out, nand_26_out, nand_27_out, nand_28_out, nand_29_out, nand_30_out,
       nand_31_out, nand_32_out, nand_33_out, nand_34_out;

  nand nand_1 (nand_1_out, sel[0], sel[0]);
  nand nand_2 (nand_2_out, sel[1], sel[1]);
  nand nand_3 (nand_3_out, in_1[0], nand_1_out);
  nand nand_4 (nand_4_out, in_1[1], nand_1_out);
  nand nand_5 (nand_5_out, in_1[2], nand_1_out);
  nand nand_6 (nand_6_out, in_1[3], nand_1_out);
  nand nand_7 (nand_7_out, in_1[0], sel[0]);
  nand nand_8 (nand_8_out, in_1[1], sel[0]);
  nand nand_9 (nand_9_out, in_1[2], sel[0]);
  nand nand_10 (nand_10_out, in_1[3], sel[0]);
  nand nand_11 (nand_11_out, nand_3_out, nand_3_out);
  nand nand_12 (nand_12_out, nand_4_out, nand_4_out);
  nand nand_13 (nand_13_out, nand_5_out, nand_5_out);
  nand nand_14 (nand_14_out, nand_6_out, nand_6_out);
  nand nand_15 (nand_15_out, nand_7_out, nand_7_out);
  nand nand_16 (nand_16_out, nand_8_out, nand_8_out);
  nand nand_17 (nand_17_out, nand_9_out, nand_9_out);
  nand nand_18 (nand_18_out, nand_10_out, nand_10_out);
  nand nand_19 (nand_19_out, nand_11_out, nand_2_out);
  nand nand_20 (nand_20_out, nand_12_out, nand_2_out);
  nand nand_21 (nand_21_out, nand_13_out, nand_2_out);
  nand nand_22 (nand_22_out, nand_14_out, nand_2_out);
  nand nand_23 (nand_23_out, nand_11_out, sel[1]);
  nand nand_24 (nand_24_out, nand_12_out, sel[1]);
  nand nand_25 (nand_25_out, nand_13_out, sel[1]);
  nand nand_26 (nand_26_out, nand_14_out, sel[1]);
  nand nand_27 (nand_27_out, nand_15_out, nand_2_out);
  nand nand_28 (nand_28_out, nand_16_out, nand_2_out);
  nand nand_29 (nand_29_out, nand_17_out, nand_2_out);
  nand nand_30 (nand_30_out, nand_18_out, nand_2_out);
  nand nand_31 (nand_31_out, nand_15_out, sel[1]);
  nand nand_32 (nand_32_out, nand_16_out, sel[1]);
  nand nand_33 (nand_33_out, nand_17_out, sel[1]);
  nand nand_34 (nand_34_out, nand_18_out, sel[1]);
  nand nand_35 (out_3[0], nand_19_out, nand_19_out);
  nand nand_36 (out_3[1], nand_20_out, nand_20_out);
  nand nand_37 (out_3[2], nand_21_out, nand_21_out);
  nand nand_38 (out_3[3], nand_22_out, nand_22_out);
  nand nand_39 (out_4[0], nand_23_out, nand_23_out);
  nand nand_40 (out_4[1], nand_24_out, nand_24_out);
  nand nand_41 (out_4[2], nand_25_out, nand_25_out);
  nand nand_42 (out_4[3], nand_26_out, nand_26_out);
  nand nand_43 (out_5[0], nand_27_out, nand_27_out);
  nand nand_44 (out_5[1], nand_28_out, nand_28_out);
  nand nand_45 (out_5[2], nand_29_out, nand_29_out);
  nand nand_46 (out_5[3], nand_30_out, nand_30_out);
  nand nand_47 (out_6[0], nand_31_out, nand_31_out);
  nand nand_48 (out_6[1], nand_32_out, nand_32_out);
  nand nand_49 (out_6[2], nand_33_out, nand_33_out);
  nand nand_50 (out_6[3], nand_34_out, nand_34_out);
endmodule

module HalfAdder (
  input  [1:0] in_1,
  input  [1:0] in_2,
  input  CarryIn,
  output Sum,
  output Carry,
  output Sum2,
  output CarryOut
);

  wire nand_1_out, nand_2_out, nand_3_out, nand_4_out, nand_5_out, nand_6_out, nand_9_out, nand_10_out,
       nand_11_out, nand_12_out;

  nand nand_1 (nand_1_out, in_1[0], in_1[1]);
  nand nand_2 (nand_2_out, in_2[0], in_2[1]);
  nand nand_3 (nand_3_out, in_1[0], nand_1_out);
  nand nand_4 (nand_4_out, nand_1_out, in_1[1]);
  nand nand_5 (nand_5_out, in_2[0], nand_2_out);
  nand nand_6 (nand_6_out, nand_2_out, in_2[1]);
  nand nand_7 (Sum, nand_3_out, nand_4_out);
  nand nand_8 (Carry, nand_1_out, nand_1_out);
  nand nand_9 (nand_9_out, nand_5_out, nand_6_out);
  nand nand_10 (nand_10_out, nand_9_out, CarryIn);
  nand nand_11 (nand_11_out, nand_9_out, nand_10_out);
  nand nand_12 (nand_12_out, nand_10_out, CarryIn);
  nand nand_13 (CarryOut, nand_2_out, nand_10_out);
  nand nand_14 (Sum2, nand_11_out, nand_12_out);
endmodule

module FullAdder4 (
  input  CarryIn,
  input  A1,
  input  B1,
  input  A2,
  input  B2,
  input  A3,
  input  B3,
  input  A4,
  input  B4,
  output Sum1,
  output Sum2,
  output Sum3,
  output Sum4,
  output CarryOut
);

  wire nand_1_out, nand_2_out, nand_3_out, nand_4_out, nand_5_out, nand_6_out, nand_7_out, nand_8_out,
       nand_9_out, nand_10_out, nand_11_out, nand_12_out, nand_13_out, nand_14_out, nand_15_out, nand_16_out,
       nand_17_out, nand_18_out, nand_19_out, nand_20_out, nand_21_out, nand_22_out, nand_23_out,
       nand_24_out, nand_25_out, nand_26_out, nand_27_out, nand_28_out, nand_29_out, nand_30_out, nand_31_out;

  nand nand_1 (nand_1_out, A1, B1);
  nand nand_2 (nand_2_out, A2, B2);
  nand nand_3 (nand_3_out, A3, B3);
  nand nand_4 (nand_4_out, A4, B4);
  nand nand_5 (nand_5_out, A1, nand_1_out);
  nand nand_6 (nand_6_out, nand_1_out, B1);
  nand nand_7 (nand_7_out, A2, nand_2_out);
  nand nand_8 (nand_8_out, nand_2_out, B2);
  nand nand_9 (nand_9_out, A3, nand_3_out);
  nand nand_10 (nand_10_out, nand_3_out, B3);
  nand nand_11 (nand_11_out, A4, nand_4_out);
  nand nand_12 (nand_12_out, nand_4_out, B4);
  nand nand_13 (nand_13_out, nand_5_out, nand_6_out);
  nand nand_14 (nand_14_out, nand_7_out, nand_8_out);
  nand nand_15 (nand_15_out, nand_9_out, nand_10_out);
  nand nand_16 (nand_16_out, nand_11_out, nand_12_out);
  nand nand_17 (nand_17_out, CarryIn, nand_13_out);
  nand nand_18 (nand_18_out, nand_23_out, nand_14_out);
  nand nand_19 (nand_19_out, nand_26_out, nand_15_out);
  nand nand_20 (nand_20_out, nand_29_out, nand_16_out);
  nand nand_21 (nand_21_out, CarryIn, nand_17_out);
  nand nand_22 (nand_22_out, nand_17_out, nand_13_out);
  nand nand_23 (nand_23_out, nand_17_out, nand_1_out);
  nand nand_24 (nand_24_out, nand_23_out, nand_18_out);
  nand nand_25 (nand_25_out, nand_18_out, nand_14_out);
  nand nand_26 (nand_26_out, nand_18_out, nand_2_out);
  nand nand_27 (nand_27_out, nand_26_out, nand_19_out);
  nand nand_28 (nand_28_out, nand_19_out, nand_15_out);
  nand nand_29 (nand_29_out, nand_19_out, nand_3_out);
  nand nand_30 (nand_30_out, nand_29_out, nand_20_out);
  nand nand_31 (nand_31_out, nand_20_out, nand_16_out);
  nand nand_32 (CarryOut, nand_20_out, nand_4_out);
  nand nand_33 (Sum1, nand_21_out, nand_22_out);
  nand nand_34 (Sum2, nand_24_out, nand_25_out);
  nand nand_35 (Sum3, nand_27_out, nand_28_out);
  nand nand_36 (Sum4, nand_30_out, nand_31_out);
endmodule
